// Logisim project rv1.circ as structural Verilog: 7 circuits, main circuit Main
module Main (
  input  rst,
  input  clk,
  output [31:0] out_3,
  output [31:0] out_4,
  output [31:0] out_5,
  output [31:0] out_6,
  output [31:0] out_7
);

  wire alu_1_condout, and_1_out, and_2_out, control_1_branch, control_1_imm, control_1_load,
       control_1_regwrite, control_1_store;
  wire [1:0] control_1_ressel, or_1_out;
  wire [3:0] control_1_alufun;
  wire [31:0] adder_1_out, adder_2_out, Data_Memory_1d562ccc_dout, multiplexer_1_out, multiplexer_3_out,
       PC_q, pcaddconst_1_constout, registers1_1_readdata1, registers1_1_readdata2;

  Register #(.width(32)) PC (.D(out_3), .clk(clk), .Q(PC_q), .clr(rst));  // open: en
  ROM #(.dataWidth(32)) InstructionMemory (.addr(PC_q[9:2]), .data(out_4));
  Adder #(.width(32)) adder_1 (.a(32'h4), .b(PC_q), .out(adder_1_out));  // open: cin, cout
  PCaddConst pcaddconst_1 (.InstrIn(out_4), .FmtSel(control_1_ressel), .ConstOut(pcaddconst_1_constout));
  Control control_1 (
    .Opcode(out_4[6:0]), .Funct3(out_4[14:12]), .Funct7(out_4[31:25]), .ResSel(control_1_ressel),
    .Jump(or_1_out[1]), .Branch(control_1_branch), .Load(control_1_load), .Store(control_1_store),
    .ALUfun(control_1_alufun), .Imm(control_1_imm), .RegWrite(control_1_regwrite));
  Registers1 registers1_1 (
    .rs1(out_4[19:15]), .rs2(out_4[24:20]), .rd(out_4[11:7]), .RegWrEn(control_1_regwrite), .clk(clk),
    .WriteData(out_6), .ReadData1(registers1_1_readdata1), .ReadData2(registers1_1_readdata2));
  ALUconst aluconst_1 (.S_format(control_1_store), .InstrIn(out_4), .ConstOut(out_7));
  and and_1 (and_1_out, out_4[3], or_1_out[1]);
  Multiplexer #(.width(32)) multiplexer_1 (
    .in0(registers1_1_readdata2), .in1(out_7), .out(multiplexer_1_out), .sel(control_1_imm));
  Adder #(.width(32)) adder_2 (.a(PC_q), .b(pcaddconst_1_constout), .out(adder_2_out));  // open: cin, cout
  and and_2 (and_2_out, control_1_branch, alu_1_condout);
  Multiplexer #(.select(2), .width(32)) multiplexer_2 (
    .in0(adder_1_out), .in1(adder_2_out), .in2(out_5), .in3(adder_2_out), .out(out_3), .sel(or_1_out));
  or or_1 (or_1_out[0], and_1_out, and_2_out);
  Multiplexer #(.select(2), .width(32)) multiplexer_3 (
    .in0(out_5), .in1(adder_1_out), .in2(pcaddconst_1_constout), .in3(adder_2_out), .out(multiplexer_3_out),
    .sel(control_1_ressel));
  ALU alu_1 (
    .fun(control_1_alufun), .in1(registers1_1_readdata1), .in2(multiplexer_1_out), .CondOut(alu_1_condout),
    .ALUout(out_5));
  RAM #(.dataWidth(32), .enables("line")) Data_Memory_1d562ccc (
    .addr(out_5[9:2]), .we(control_1_store), .clk(clk), .din(registers1_1_readdata2),
    .dout(Data_Memory_1d562ccc_dout));
  Multiplexer #(.width(32)) multiplexer_4 (
    .in0(multiplexer_3_out), .in1(Data_Memory_1d562ccc_dout), .out(out_6), .sel(control_1_load));

  // Notes on the sheet:
  //   contents of InstructionMemory (hex, n*v repeats v):
  //   a00513 5b3 259613 2062683 b686b3 2d62023 158593 fea5e6e3 fe0002e3
  //   PC incrementer
  //   Instruction Memory
  //   nextPC
  //   currPC
  //   JAL
  //   PC adder
  //   Data Memory
endmodule

module Registers1 (
  input  [4:0] rs1,
  input  [4:0] rs2,
  input  [4:0] rd,
  input  RegWrEn,
  input  clk,
  input  [31:0] WriteData,
  output [31:0] ReadData1,
  output [31:0] ReadData2
);

  wire and_1_out, comparator_1_gt;
  wire [4:0] multiplexer_1_out, multiplexer_2_out;
  wire [31:0] r1_dout, ram_1_dout;

  Comparator #(.width(5)) comparator_1 (.a(rd), .b({5{1'b0}}), .gt(comparator_1_gt));  // open: eq, lt
  and and_1 (and_1_out, comparator_1_gt, RegWrEn);
  RAM #(.addrWidth(5), .dataWidth(32), .enables("line")) r1 (
    .addr(multiplexer_1_out), .we(and_1_out), .clk(clk), .din(WriteData), .dout(r1_dout));
  Multiplexer #(.width(5)) multiplexer_1 (.in0(rd), .in1(rs1), .out(multiplexer_1_out), .sel(clk));
  RAM #(.addrWidth(5), .dataWidth(32), .enables("line")) ram_1 (
    .addr(multiplexer_2_out), .we(and_1_out), .clk(clk), .din(WriteData), .dout(ram_1_dout));
  Multiplexer #(.width(5)) multiplexer_2 (.in0(rd), .in1(rs2), .out(multiplexer_2_out), .sel(clk));
  Register #(.trigger("high"), .width(32)) register_1 (.D(r1_dout), .clk(clk), .Q(ReadData1));  // open: en, clr
  Register #(.trigger("high"), .width(32)) register_2 (.D(ram_1_dout), .clk(clk), .Q(ReadData2));  // open: en, clr
endmodule

module Const (
  input  [2:0] ConstFmt,
  input  [31:0] InstrIn,
  output [31:0] ConstOut
);

  wire [31:0] bit_extender_1_out, bit_extender_2_out, bit_extender_3_out, bit_extender_4_out;

  assign bit_extender_1_out = {{20{InstrIn[31]}}, InstrIn[31:20]};  // Bit_Extender bit_extender_1
  assign bit_extender_2_out = {{20{InstrIn[31]}}, {InstrIn[31:25], InstrIn[11:7]}};  // Bit_Extender bit_extender_2
  assign bit_extender_3_out = {{19{InstrIn[31]}}, {InstrIn[31], InstrIn[7], InstrIn[30:25], InstrIn[11:8], 1'b0}};  // Bit_Extender bit_extender_3
  assign bit_extender_4_out = {{11{InstrIn[31]}}, {InstrIn[31], InstrIn[19:12], InstrIn[20], InstrIn[30:21], 1'b0}};  // Bit_Extender bit_extender_4
  Multiplexer #(.select(3), .width(32)) multiplexer_1 (
    .in0(bit_extender_1_out), .in1(bit_extender_2_out), .in2(bit_extender_3_out),
    .in3({InstrIn[31:12], {12{1'b0}}}), .in4(bit_extender_4_out), .out(ConstOut), .sel(ConstFmt));  // open: in5, in6, in7

  // Notes on the sheet:
  //   Imm
  //   Store
  //   Branch
  //   Upper
  //   Jump
endmodule

module ALU (
  input  [3:0] fun,
  input  [31:0] in1,
  input  [31:0] in2,
  output CondOut,
  output [31:0] ALUout
);

  wire comparator_1_eq, comparator_1_lt, comparator_2_lt, multiplexer_3_out;
  wire [31:0] adder_1_out, and_1_out, bit_extender_1_out, bit_extender_2_out, multiplexer_1_out,
       multiplexer_2_out, or_1_out, shifter_1_out, shifter_2_out, shifter_3_out, subtractor_1_out, xor_1_out;

  Adder #(.width(32)) adder_1 (.a(in1), .b(in2), .out(adder_1_out));  // open: cin, cout
  Subtractor #(.width(32)) subtractor_1 (.a(in1), .b(in2), .out(subtractor_1_out));  // open: bin, bout
  Multiplexer #(.width(32)) multiplexer_1 (
    .in0(adder_1_out), .in1(subtractor_1_out), .out(multiplexer_1_out), .sel(fun[3]));
  Shifter #(.width(32)) shifter_1 (.in(in1), .\dist (in2[4:0]), .out(shifter_1_out));
  Comparator #(.width(32)) comparator_1 (.a(in1), .b(in2), .eq(comparator_1_eq), .lt(comparator_1_lt));  // open: gt
  Comparator #(.mode("unsigned"), .width(32)) comparator_2 (.a(in1), .b(in2), .lt(comparator_2_lt));  // open: gt, eq
  assign xor_1_out = in1 ^ in2;  // XOR_Gate xor_1, 32 bits wide
  Shifter #(.shift("lr"), .width(32)) shifter_2 (.in(in1), .\dist (in2[4:0]), .out(shifter_2_out));
  Shifter #(.shift("ar"), .width(32)) shifter_3 (.in(in1), .\dist (in2[4:0]), .out(shifter_3_out));
  assign or_1_out = in1 | in2;  // OR_Gate or_1, 32 bits wide
  assign and_1_out = in1 & in2;  // AND_Gate and_1, 32 bits wide
  Multiplexer #(.width(32)) multiplexer_2 (
    .in0(shifter_2_out), .in1(shifter_3_out), .out(multiplexer_2_out), .sel(fun[3]));
  xor xor_2 (CondOut, fun[0], multiplexer_3_out);
  Multiplexer #(.select(2)) multiplexer_3 (
    .in0(comparator_1_eq), .in1(1'b0), .in2(comparator_1_lt), .in3(comparator_2_lt), .out(multiplexer_3_out),
    .sel(fun[2:1]));
  assign bit_extender_1_out = {{31{1'b0}}, comparator_1_lt};  // Bit_Extender bit_extender_1
  assign bit_extender_2_out = {{31{1'b0}}, comparator_2_lt};  // Bit_Extender bit_extender_2
  Multiplexer #(.select(3), .width(32)) multiplexer_4 (
    .in0(multiplexer_1_out), .in1(shifter_1_out), .in2(bit_extender_1_out), .in3(bit_extender_2_out),
    .in4(xor_1_out), .in5(multiplexer_2_out), .in6(or_1_out), .in7(and_1_out), .out(ALUout), .sel(fun[2:0]));

  // Notes on the sheet:
  //   ADD
  //   SUB
  //   SLL
  //   SLT
  //   SLTU
endmodule

module Control (
  input  [6:0] Opcode,
  input  [2:0] Funct3,
  input  [6:0] Funct7,
  output [1:0] ResSel,
  output Jump,
  output Branch,
  output Load,
  output Store,
  output [3:0] ALUfun,
  output Imm,
  output RegWrite
);

  wire not_1_out;
  wire [11:5] DecodeROM_data;

  ROM #(.addrWidth(5), .dataWidth(12)) DecodeROM (
    .addr(Opcode[6:2]),
    .data({DecodeROM_data[11:8], ResSel, DecodeROM_data[5], RegWrite, Imm, Store, Load, Branch}));
  Multiplexer #(.width(4)) multiplexer_1 (
    .in0(4'b0000), .in1({Funct7[5], Funct3}), .out(ALUfun), .sel(DecodeROM_data[5]));
  not not_1 (not_1_out, ResSel[1]);
  and and_1 (Jump, ResSel[0], not_1_out);

  // Notes on the sheet:
  //   contents of DecodeROM (hex, n*v repeats v):
  //   1a 0 0 0 38 d0 0 0 c 0 0 0 30 90 10*0 21 50 0 50
endmodule

module ALUconst (
  input  S_format,
  input  [31:0] InstrIn,
  output [31:0] ConstOut
);

  wire [11:0] multiplexer_1_out;

  Multiplexer #(.width(12)) multiplexer_1 (
    .in0(InstrIn[31:20]), .in1({InstrIn[31:25], InstrIn[11:7]}), .out(multiplexer_1_out), .sel(S_format));
  assign ConstOut = {{20{multiplexer_1_out[11]}}, multiplexer_1_out};  // Bit_Extender bit_extender_1

  // Notes on the sheet:
  //   Imm
  //   Store
endmodule

module PCaddConst (
  input  [31:0] InstrIn,
  input  [1:0] FmtSel,
  output [31:0] ConstOut
);

  wire [31:0] bit_extender_1_out, bit_extender_2_out;

  assign bit_extender_1_out = {{19{InstrIn[31]}}, {InstrIn[31], InstrIn[7], InstrIn[30:25], InstrIn[11:8], 1'b0}};  // Bit_Extender bit_extender_1
  assign bit_extender_2_out = {{11{InstrIn[31]}}, {InstrIn[31], InstrIn[19:12], InstrIn[20], InstrIn[30:21], 1'b0}};  // Bit_Extender bit_extender_2
  Multiplexer #(.select(2), .width(32)) multiplexer_1 (
    .in0(bit_extender_1_out), .in1(bit_extender_2_out), .in2({InstrIn[31:12], {12{1'b0}}}),
    .in3({InstrIn[31:12], {12{1'b0}}}), .out(ConstOut), .sel(FmtSel));

  // Notes on the sheet:
  //   Jump
  //   Upper
  //   Branch
endmodule
